# Fritzing sketch foos_RPi_only (saved by Fritzing 0.9.3b)
breadboards: 1

parts:
  Raspberry_Pi_1 = Raspberry Pi 3 [part_number=RPI-3-V1.2]
  R2 = Resistor [tolerance=±5% resistance=330 package="0805 [SMD]"]
  IR1 = TSOP312.., 314.. [package=THT]
  R1 = Resistor [tolerance=±5% resistance=10k package="0805 [SMD]"]
  R3 = Resistor [tolerance=±5% resistance=330 package="0805 [SMD]"]
  LED1 = smd LED [color="Infrared (940nm)" package="1206 [SMD]"]
  LED2 = smd LED [color="Infrared (940nm)" package="1206 [SMD]"]
  IR2 = TSOP312.., 314.. [package=THT]
  Yellow+ = SWITCH-MOMENTARY-2 [package=tactile-pth-12mm]
  Yellow- = SWITCH-MOMENTARY-2 [package=tactile-pth-12mm]
  Black- = SWITCH-MOMENTARY-2 [package=tactile-pth-12mm]
  Black+ = SWITCH-MOMENTARY-2 [package=tactile-pth-12mm]
  Ok = SWITCH-MOMENTARY-2 [package=tactile-pth-12mm]
  Q2 = NPN-Transistor [package="TO92 [THT]"]

nets:
  N1: Raspberry_Pi_1.GPIO2, Black+.2
  GND: Raspberry_Pi_1.GND, IR1.GND, IR2.GND, Yellow+.2, Yellow-.2, Black-.2, Black+.1, Ok.2, Q2.E
  N2: Raspberry_Pi_1.GIPO7, IR1.Data
  N3: Raspberry_Pi_1.GIPO8, Ok.1
  N4: Raspberry_Pi_1.GIPO25, Black-.1
  N5: Raspberry_Pi_1.GIPO23, Yellow-.1
  N6: Raspberry_Pi_1.GIPO18, R1.Pin_1
  N7: Raspberry_Pi_1.GIPO15, Yellow+.1
  N8: Raspberry_Pi_1.GIPO14, IR2.Data
  N9: Raspberry_Pi_1.5V, R2.Pin_1, IR1.Vs, R3.Pin_1, IR2.Vs
  N10: R2.Pin_0, LED1.anode
  N11: R1.Pin_0, Q2.B
  N12: R3.Pin_0, LED2.anode
  N13: LED1.cathode, LED2.cathode, Q2.C
