# Fritzing sketch foos_arduino (saved by Fritzing 0.9.3b)
breadboards: 1

parts:
  Part1 = Arduino Nano (Rev3.0)
  R2 = Resistor [tolerance=±5% resistance=330 package=THT]
  R6 = Resistor [tolerance=±5% resistance=330 package=THT]
  R7 = Resistor [tolerance=±5% resistance=10k package=THT]
  IR1 = TSOP312.., 314.. [package=THT]
  LED1 = smd LED [color="Infrared (940nm)" package="0805 [SMD]"]
  S1 = Round Pushbutton
  LED3 = smd LED [color="Red (633nm)" package="0805 [SMD]"]
  LED4 = smd LED [color="Infrared (940nm)" package="0805 [SMD]"]
  R8 = Resistor [tolerance=±5% resistance=330 package=THT]
  R9 = Resistor [tolerance=±5% resistance=330 package=THT]
  S2 = Round Pushbutton
  LED5 = smd LED [color="Red (633nm)" package="0805 [SMD]"]
  R10 = Resistor [tolerance=±5% resistance=330 package=THT]
  S3 = Round Pushbutton
  LED6 = smd LED [color="Red (633nm)" package="0805 [SMD]"]
  R11 = Resistor [tolerance=±5% resistance=330 package=THT]
  S4 = Round Pushbutton
  LED7 = smd LED [color="Red (633nm)" package="0805 [SMD]"]
  R12 = Resistor [tolerance=±5% resistance=330 package=THT]
  S5 = Round Pushbutton
  LED8 = smd LED [color="Red (633nm)" package="0805 [SMD]"]
  R13 = Resistor [tolerance=±5% resistance=100 package=THT]
  R14 = Resistor [tolerance=±5% resistance=100 package=THT]
  C1 = Ceramic Capacitor [capacitance=100nF package="100 mil [THT, multilayer]"]
  C2 = Ceramic Capacitor [capacitance=100nF package="100 mil [THT, multilayer]"]
  IR2 = TSOP312.., 314.. [package=THT]
  Q2 = NPN-Transistor [package="TO92 [THT]"]

nets:
  GND: Part1.GND, IR1.GND, S1.leg1, LED3.cathode, S2.leg1, LED5.cathode, S3.leg1, LED6.cathode, S4.leg1, LED7.cathode, S5.leg1, LED8.cathode, C1.0, C2.0, IR2.GND, Q2.E
  N1: Part1.D2, S1.leg0
  N2: Part1.D3, S2.leg0
  N3: Part1.D4, S3.leg0
  N4: Part1.D5, S4.leg0
  N5: Part1.D6, S5.leg0
  N6: Part1.D9, R7.Pin_0
  N7: Part1.D10, IR1.Data
  N8: Part1.D11/MOSI, IR2.Data
  N9: Part1.5V, R6.Pin_0, R8.Pin_0, R13.Pin_0, R14.Pin_0
  N10: Part1.A4, R12.Pin_1
  N11: Part1.A3, R11.Pin_1
  N12: Part1.A2, R10.Pin_1
  N13: Part1.A1, R9.Pin_1
  N14: Part1.A0, R2.Pin_1
  N15: R2.Pin_0, LED3.anode
  N16: R6.Pin_1, LED1.anode
  N17: R7.Pin_1, Q2.B
  N18: IR1.Vs, R14.Pin_1, C2.1
  N19: LED1.cathode, LED4.cathode, Q2.C
  N20: LED4.anode, R8.Pin_1
  N21: R9.Pin_0, LED5.anode
  N22: R10.Pin_0, LED6.anode
  N23: R11.Pin_0, LED7.anode
  N24: R12.Pin_0, LED8.anode
  N25: R13.Pin_1, C1.1, IR2.Vs

notes:
  Pushbutton with LED x5
  IR Barrier x2
  USB to RPi
