# Fritzing sketch foos_arduino_micro (saved by Fritzing 0.9.3b)
breadboards: 1

parts:
  R2 = Resistor [tolerance=±5% resistance=330 package=THT]
  R6 = Resistor [tolerance=±5% resistance=330 package=THT]
  R7 = Resistor [tolerance=±5% resistance=10k package=THT]
  IR1 = TSOP312.., 314.. [package=THT]
  LED1 = smd LED [color="Infrared (940nm)" package="0805 [SMD]"]
  S1 = Round Pushbutton
  LED3 = smd LED [color="Red (633nm)" package="0805 [SMD]"]
  LED4 = smd LED [color="Infrared (940nm)" package="0805 [SMD]"]
  R8 = Resistor [tolerance=±5% resistance=330 package=THT]
  R9 = Resistor [tolerance=±5% resistance=330 package=THT]
  S2 = Round Pushbutton
  LED5 = smd LED [color="Red (633nm)" package="0805 [SMD]"]
  R10 = Resistor [tolerance=±5% resistance=330 package=THT]
  S3 = Round Pushbutton
  LED6 = smd LED [color="Red (633nm)" package="0805 [SMD]"]
  R11 = Resistor [tolerance=±5% resistance=330 package=THT]
  S4 = Round Pushbutton
  LED7 = smd LED [color="Red (633nm)" package="0805 [SMD]"]
  R12 = Resistor [tolerance=±5% resistance=330 package=THT]
  S5 = Round Pushbutton
  LED8 = smd LED [color="Red (633nm)" package="0805 [SMD]"]
  R13 = Resistor [tolerance=±5% resistance=100 package=THT]
  R14 = Resistor [tolerance=±5% resistance=100 package=THT]
  C1 = Ceramic Capacitor [capacitance=100nF package="100 mil [THT, multilayer]"]
  C2 = Ceramic Capacitor [capacitance=100nF package="100 mil [THT, multilayer]"]
  IR2 = TSOP312.., 314.. [package=THT]
  Q2 = NPN-Transistor [package="TO92 [THT]"]
  Part2 = Arduino Micro (Rev3)

nets:
  N1: R2.Pin_0, LED3.anode
  N2: R2.Pin_1, Part2.A0
  N3: R6.Pin_0, R8.Pin_0, R13.Pin_0, R14.Pin_0, Part2.5V
  N4: R6.Pin_1, LED1.anode
  N5: R7.Pin_0, Part2.D9_PWM/A9
  N6: R7.Pin_1, Q2.B
  GND: IR1.GND, S1.leg1, LED3.cathode, S2.leg1, LED5.cathode, S3.leg1, LED6.cathode, S4.leg1, LED7.cathode, S5.leg1, LED8.cathode, C1.0, C2.0, IR2.GND, Q2.E, Part2.GND
  N7: IR1.Vs, R14.Pin_1, C2.1
  N8: IR1.Data, Part2.D10_PWM/A10
  N9: LED1.cathode, LED4.cathode, Q2.C
  N10: S1.leg0, Part2.D2/SDA
  N11: LED4.anode, R8.Pin_1
  N12: R9.Pin_0, LED5.anode
  N13: R9.Pin_1, Part2.A1
  N14: S2.leg0, Part2.D3/SCL
  N15: R10.Pin_0, LED6.anode
  N16: R10.Pin_1, Part2.A2
  N17: S3.leg0, Part2.D4_PWM/A6
  N18: R11.Pin_0, LED7.anode
  N19: R11.Pin_1, Part2.A3
  N20: S4.leg0, Part2.D5_PWM
  N21: R12.Pin_0, LED8.anode
  N22: R12.Pin_1, Part2.A4
  N23: S5.leg0, Part2.D6_PWM/A7
  N24: R13.Pin_1, C1.1, IR2.Vs
  N25: IR2.Data, Part2.D11_PWM

notes:
  Pushbutton with LED x5
  IR Barrier x2
  USB to RPi
