# Fritzing sketch micro_breakbeam (saved by Fritzing 0.9.3b)
breadboards: 1

parts:
  R2 = Resistor [tolerance=±5% resistance=330 package=THT]
  S1 = Round Pushbutton
  OK = smd LED [color="Red (633nm)" package="0805 [SMD]"]
  R9 = Resistor [tolerance=±5% resistance=330 package=THT]
  BI = smd LED [color="Red (633nm)" package="0805 [SMD]"]
  R10 = Resistor [tolerance=±5% resistance=330 package=THT]
  S3 = Round Pushbutton
  BD = smd LED [color="Red (633nm)" package="0805 [SMD]"]
  R11 = Resistor [tolerance=±5% resistance=330 package=THT]
  S4 = Round Pushbutton
  YD = smd LED [color="Red (633nm)" package="0805 [SMD]"]
  R12 = Resistor [tolerance=±5% resistance=330 package=THT]
  S5 = Round Pushbutton
  YI = smd LED [color="Red (633nm)" package="0805 [SMD]"]
  S2 = Round Pushbutton
  Adafruit_Breakbeam_Sensor = TSOP312.., 314.. [package=THT]
  Adafruit_Breakbeam_Sensor1 = TSOP312.., 314.. [package=THT]
  Adafruit_IR_LED = smd LED [color="Infrared (850nm)" package="0805 [SMD]"]
  Adafruit_IR_LED1 = smd LED [color="Infrared (850nm)" package="0805 [SMD]"]
  Part2 = Arduino Micro (Rev3)

nets:
  N1: R2.Pin_0, OK.anode
  N2: R2.Pin_1, Part2.A0
  N3: S1.leg0, Part2.D8_PWM/A8
  N4: S1.leg1, OK.cathode, BI.cathode, S3.leg1, BD.cathode, S4.leg1, YD.cathode, S5.leg1, YI.cathode, S2.leg1
  N5: R9.Pin_0, BI.anode
  N6: R9.Pin_1, Part2.A1
  N7: R10.Pin_0, BD.anode
  N8: R10.Pin_1, Part2.A2
  N9: S3.leg0, Part2.D6_PWM/A7
  N10: R11.Pin_0, YD.anode
  N11: R11.Pin_1, Part2.A3
  N12: S4.leg0, Part2.D5_PWM
  N13: R12.Pin_0, YI.anode
  N14: R12.Pin_1, Part2.A4
  N15: S5.leg0, Part2.D4_PWM/A6
  N16: S2.leg0, Part2.D7
  GND: Adafruit_Breakbeam_Sensor.GND, Adafruit_Breakbeam_Sensor1.GND, Adafruit_IR_LED.cathode, Adafruit_IR_LED1.cathode, Part2.GND
  N17: Adafruit_Breakbeam_Sensor.Vs, Part2.5V
  N18: Adafruit_Breakbeam_Sensor.Data, Part2.D10_PWM/A10
  N19: Adafruit_Breakbeam_Sensor1.Vs, Adafruit_IR_LED.anode, Adafruit_IR_LED1.anode
  N20: Adafruit_Breakbeam_Sensor1.Data, Part2.D11_PWM

notes:
  Pushbuttons with LED x5
  IR Barrier x2
  USB to RPi
